# Fritzing sketch kettle (saved by Fritzing 1.0.4)
circuit board: 2cm x 11cm
breadboards: 2

parts:
  10K2 = Rotary Potentiometer (Small) [maximum_resistance=1MΩ knob_status=50% power=0.5W package=THT]
  10K1 = Rotary Potentiometer (Small) [maximum_resistance=10kΩ knob_status=50% power=0.5W package=THT]
  IN1 = PJ-301M [part_number=PJ-301M]
  104 = Ceramic Capacitor [capacitance=100nF voltage=16V package="200 mil [THT, multilayer]"]
  IN2 = PJ-301M [part_number=PJ-301M]
  Out1 = PJ-301M [part_number=PJ-301M]
  IN3 = PJ-301M [part_number=PJ-301M]
  IN4 = PJ-301M [part_number=PJ-301M]
  10K3 = Rotary Potentiometer (Small) [maximum_resistance=1MΩ knob_status=50% power=0.5W package=THT]
  10K4 = Rotary Potentiometer (Small) [maximum_resistance=1MΩ knob_status=50% power=0.5W package=THT]
  Out2 = PJ-301M [part_number=PJ-301M]
  J3 = shrouded pin header, 10 pins [form="♂ (shrouded male)"]
  100uF = Electrolytic Capacitor [capacitance=0.1mF voltage=35V package="100 mil [THT, electrolytic]"]
  4_7K = Resistor [tolerance=±1% power=0.25W resistance=10k package=THT]
  1K = Resistor [tolerance=±1% power=0.25W resistance=1k package=THT]
  4_7K_2 = Resistor [tolerance=±1% power=0.25W resistance=4.7k package=THT]
  4001 = Diode [package=diode-1n4148]
  1K1 = Resistor [tolerance=±1% power=0.25W resistance=1k package=THT]
  1K_2 = Resistor [tolerance=±1% power=0.25W resistance=1k package=THT]
  1K_3 = Resistor [tolerance=±1% power=0.25W resistance=1k package=THT]
  OPA2135 = TL072 [package="DIP (Dual Inline) [THT]"]
  OPA2135_PWR = TL072 [package="DIP (Dual Inline) [THT]"]  # not connected
  OPA2135_A = TL072 [package="DIP (Dual Inline) [THT]"]  # not connected
  OPA2135_B = TL072 [package="DIP (Dual Inline) [THT]"]  # not connected
  072 = TL072 [package="DIP (Dual Inline) [THT]"]
  072_PWR = TL072 [package="DIP (Dual Inline) [THT]"]  # not connected
  072_A = TL072 [package="DIP (Dual Inline) [THT]"]  # not connected
  072_B = TL072 [package="DIP (Dual Inline) [THT]"]  # not connected
  4_7K_3 = Resistor [tolerance=±1% power=0.25W resistance=4.7k package=THT]
  4_7K_4 = Resistor [tolerance=±1% power=0.25W resistance=4.7k package=THT]
  J5 = female pin header, 1 pin [form="♀ (female)"]

nets:
  GND: 10K2.leg1, 10K1.leg1, IN1.Pin_1, 104.1, Out1.Pin_1, IN3.Pin_1, IN4.Pin_1, 10K3.leg1, 10K4.leg1, Out2.Pin_1, J3.pin2, J3.pin3, J3.pin4, J3.pin7, J3.pin8, J3.pin9, 100uF.-, OPA2135.connector2, OPA2135.connector3, 072.connector2, 072.connector3, 072.connector4, J5.pin1
  N1: 10K2.wiper, 10K1.wiper, Out1.Pin_3
  N2: 10K2.leg2, 4_7K_2.Pin_0, OPA2135.connector0
  N3: 10K1.leg2, 4_7K.Pin_1, OPA2135.connector6
  N4: IN1.Pin_3, 1K_3.Pin_1
  N5: 104.0, 100uF.+, 4001.C, OPA2135.connector4
  N6: IN2.Pin_3, 1K.Pin_1
  N7: IN3.Pin_3, 1K1.Pin_1
  N8: IN4.Pin_3, 1K_2.Pin_1
  N9: 10K3.wiper, 10K4.wiper, Out2.Pin_3
  N10: 10K3.leg2, 072.connector6, 4_7K_3.Pin_1
  N11: 10K4.leg2, 072.connector0, 4_7K_4.Pin_0
  N12: J3.pin1, J3.pin10
  N13: J3.pin5, J3.pin6, 4001.A
  N14: 4_7K.Pin_0, 1K_3.Pin_0, OPA2135.connector5
  N15: 1K.Pin_0, 4_7K_2.Pin_1, OPA2135.connector1
  N16: 1K1.Pin_0, 072.connector5, 4_7K_3.Pin_0
  N17: 1K_2.Pin_0, 072.connector1, 4_7K_4.Pin_1

notes:
  kettle
  blueprint@poetaster . de
  jlcjlcjlcjlcjlc

custom parts:
  PJ-301M: Phone power jack.
  TL072: Dual Operational Amplifier
  TL072: Dual Operational Amplifier
  TL072: Dual Operational Amplifier
  TL072: Dual Operational Amplifier
